# Fritzing sketch schematic (saved by Fritzing 0.9.10b)

parts:
  Mod1 = Raspberry Pi Pico
  U1 = IC, DIP package, 8 pins [chip_label=TDA7267]
  R1 = Vertical Resistor [tolerance=±5% resistance=15000 package=THT]
  C5 = Electrolytic Capacitor top view [capacitance=4.7µF voltage=35V package="100 mil [THT, electrolytic]"]
  Loudspeaker = female pin header, 2 pins [form="♀ (female)"]
  Volume_Poti = female pin header, 3 pins [form="♀ (female)"]
  C4 = Electrolytic Capacitor top view [capacitance=0.47mF voltage=35V package="100 mil [THT, electrolytic]"]
  C6 = Ceramic Capacitor [capacitance="100 nF" voltage=35V package="1206 [SMD]"]
  C7 = Electrolytic Capacitor top view [capacitance=0.1mF voltage=35V package="100 mil [THT, electrolytic]"]
  MRF_3_3V = female pin header, 1 pin [form="♀ (female)"]
  DEBO_MICROSD_v3 = female pin header, 6 pins [form="♀ (female)"]
  MRF_RST = female pin header, 1 pin [form="♀ (female)"]
  MRF_GND = female pin header, 1 pin [form="♀ (female)"]
  MRF_MISO = female pin header, 1 pin [form="♀ (female)"]
  MRF_MOSI = female pin header, 1 pin [form="♀ (female)"]
  MRF_SCK = female pin header, 1 pin [form="♀ (female)"]
  MRF_SDA = female pin header, 1 pin [form="♀ (female)"]
  S1 = SWITCH-MOMENTARY-2 [package=tactile-switch-1101ne]
  LED1 = LED - 3mm [color="Red (633nm)" current=0.20A package="3 mm [THT]"]
  R3 = Vertical Resistor [tolerance=±5% resistance=100 package=THT]

nets:
  N1: Mod1.pin_1, DEBO_MICROSD_v3.pin5
  N2: Mod1.pin_2, DEBO_MICROSD_v3.pin2
  GND: Mod1.pin_3, Mod1.pin_8, Mod1.pin_13, Mod1.pin_18, Mod1.pin_38, U1.pin5, U1.pin6, U1.pin7, U1.pin8, C5.-, Loudspeaker.pin2, Volume_Poti.pin1, C7.-, DEBO_MICROSD_v3.pin6, MRF_GND.pin1, S1.1, LED1.cathode
  N3: Mod1.pin_4, DEBO_MICROSD_v3.pin4
  N4: Mod1.pin_5, DEBO_MICROSD_v3.pin3
  N5: Mod1.pin_7, S1.2
  N6: Mod1.pin_10, MRF_RST.pin1
  N7: Mod1.pin_11, MRF_MISO.pin1
  N8: Mod1.pin_12, MRF_SDA.pin1
  N9: Mod1.pin_14, MRF_SCK.pin1
  N10: Mod1.pin_15, MRF_MOSI.pin1
  N11: Mod1.pin_20, R3.Pin_1
  N12: Mod1.pin_25, R1.Pin_0
  N13: Mod1.pin_34, U1.pin3, C5.+
  N14: Mod1.pin_36, MRF_3_3V.pin1, DEBO_MICROSD_v3.pin1
  N15: Mod1.pin_40, U1.pin1, C7.+
  N16: U1.pin2, C4.+
  N17: U1.pin4, C6.1
  N18: R1.Pin_1, Volume_Poti.pin3
  N19: Loudspeaker.pin1, C4.-
  N20: Volume_Poti.pin2, C6.0
  N21: LED1.anode, R3.Pin_0

custom parts:
  Raspberry Pi Pico: Raspberry Pi Pico. Based around the RP2040 microcontroller the Pico is a low cost microcontroller device bringing Raspberry Pi quality, cost, and easy of use to the microcontroller space. Jan 2021, Split part in to two versions: tht (this one) and SMD. This one will drill holes for a .1 in header in pcb to allow plugging in the module as well as providing pads to solder the module to the top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
  Vertical Resistor: A generic resistor (0.25W)
  Electrolytic Capacitor top view: A small electrolytic capacitor breadboard top view for use on perf board
  Ceramic Capacitor: 0.01 nF multilayered Ceramic Capacitor
